# Fritzing sketch dataMandala-arduino (saved by Fritzing 0.9.4)
breadboards: 1

parts:
  Part8 = Arduino Uno (Rev3) - ICSP
  Mod1 = KY-015 Temperature & Humidity Sensor Module [package="Breakout board"]
  Mod2 = KY-026 Flame Sensor Module [package="Breakout board"]

nets:
  N1: Part8.A0, Mod2.A0
  N2: Part8.D2, Mod1.S
  5V: Part8.5V, Mod1.Vin, Mod2.+
  N3: Part8.GND, Mod1.-, Mod2.G

custom parts:
  KY-015 Temperature & Humidity Sensor Module: KY-015 temperature and humidity sensor module, provides a low-latency serial interface to measure humidity and temperature.
  KY-026 Flame Sensor Module: KY-026 Flame Sensor Module reacts in the presence of fire.
